# Fritzing sketch Final_Circuit (saved by Fritzing 0.9.3b)
breadboards: 1

parts:
  Part1 = Arduino Nano (Rev3.0)
  J1 = Basic Servo
  J3 = Basic Servo
  SEN1 = Pulse Sensor [package=SIP-3]
  A1 = Sparkfun myroware muscle sensor V1
  J2 = Basic Servo

nets:
  GND: Part1.GND, J1.gnd, J3.gnd, SEN1.GND, A1.Pin_8, J2.gnd
  N1: Part1.D3, J2.pulse
  N2: Part1.D4, J1.pulse
  N3: Part1.D5, J3.pulse
  VCC: Part1.5V, J1.vcc, J3.vcc, SEN1.VCC, A1.Pin_9, J2.vcc
  N4: Part1.A1, A1.Pin_7
  N5: Part1.A0, SEN1.Signal

notes:
  Crown servo
  Left servo
  Right servo

custom parts:
  Pulse Sensor: Pulse Sensor Optical Heart Beat Sensor
  Sparkfun myroware muscle sensor V1: The MyoWare Muscle Sensor is the latest revision of the Muscle Sensor of old, now with a new wearable design that allows you to attach biomedical sensor pads directly to the board itself getting rid of those pesky cables. This new board also includes a slew of other new features including, single-supply voltage of +3.1V to +5V, RAW EMG output, polarity protected power pins, indicator LEDs, and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
